// Logisim project TP-Processeur-final.circ as structural Verilog: 10 circuits, main circuit main
module main (
);

  wire CLOCK_out;
  wire [2:0] counter_1_q;
  wire [25:0] rom_1_data;

  Counter #(.width(3), .max('h7)) counter_1 (
    .D(counter_1_q), .Q(counter_1_q), .clk(CLOCK_out));  // open: load, count, carry, clr
  ROM #(.addrWidth(3), .dataWidth(26)) rom_1 (.addr(counter_1_q), .data(rom_1_data), .sel(1'b1));
  Clock CLOCK (.out(CLOCK_out));
  PROCESSOR Processeur (
    .WRITE_REG(rom_1_data[3:0]), .Adress_RAM(rom_1_data[7:4]), .Clock(CLOCK_out),
    .SELECT_INPUT_REG(rom_1_data[9:8]), .Choix_registre_input(rom_1_data[11:10]), .RESET(rom_1_data[15:12]),
    .ENABLE_WRITE_REGISTER(rom_1_data[16]), .SELECTION_OUTPUT_1(rom_1_data[18:17]),
    .SELECTION_OUTPUT_2(rom_1_data[20:19]), .OPERATIONS(rom_1_data[22:21]), .Enable_RAM(rom_1_data[23]),
    .load_RAM(rom_1_data[24]), .clear_RAM(rom_1_data[25]));

  // Notes on the sheet:
  //   contents of rom_1 (hex, n*v repeats v):
  //   1010201 1010602 1010a03 810d00 16f0800 840040 1000000 1f800
endmodule

module ADD_1BIT (
  input  A,
  input  B,
  input  Cin,
  output S,
  output Cout
);

  wire and_1_out, and_2_out, and_3_out, xor_1_out;

  xor xor_1 (xor_1_out, A, B);
  and and_1 (and_1_out, A, B);
  and and_2 (and_2_out, B, Cin);
  and and_3 (and_3_out, A, Cin);
  xor xor_2 (S, xor_1_out, Cin);
  or or_1 (Cout, and_1_out, and_2_out, and_3_out);
endmodule

// OR
module OR_4BITS (
  input  [3:0] A,
  input  [3:0] B,
  output [3:0] S1
);

  assign S1 = A | B;  // OR_Gate or_1, 4 bits wide
endmodule

// AND
module AND_4BITS (
  input  [3:0] A,
  input  [3:0] B,
  output [3:0] S1
);

  assign S1 = A & B;  // AND_Gate and_1, 4 bits wide

  // Notes on the sheet:
  //   AND
endmodule

// XOR
module XOR_4BITS (
  input  [3:0] A,
  input  [3:0] B,
  output [3:0] S1
);

  assign S1 = A ^ B;  // XOR_Gate xor_1, 4 bits wide

  // Notes on the sheet:
  //   XOR
endmodule

// ADD
module ADD_4BITS (
  input  C_in,
  input  [3:0] A,
  input  [3:0] B,
  output [3:0] S,
  output C_out
);

  wire ADD_BIT1_cout, ADD_BIT2_cout, ADD_BIT3_cout;

  ADD_1BIT ADD_BIT1 (.A(A[0]), .B(B[0]), .Cin(C_in), .S(S[0]), .Cout(ADD_BIT1_cout));
  ADD_1BIT ADD_BIT2 (.A(A[1]), .B(B[1]), .Cin(ADD_BIT1_cout), .S(S[1]), .Cout(ADD_BIT2_cout));
  ADD_1BIT ADD_BIT3 (.A(A[2]), .B(B[2]), .Cin(ADD_BIT2_cout), .S(S[2]), .Cout(ADD_BIT3_cout));
  ADD_1BIT ADD_BIT4 (.A(A[3]), .B(B[3]), .Cin(ADD_BIT3_cout), .S(S[3]), .Cout(C_out));

  // Notes on the sheet:
  //   Additionneur 4 bits
endmodule

// UAL
module UAL_4BITS (
  input  [1:0] OPERATIONS,
  input  [3:0] A,
  input  [3:0] B,
  input  Carry_Flag,
  output [3:0] S1,
  output Carry_Flag_2
);

  wire [3:0] add_4bits_1_s, and_4bits_1_s1, or_4bits_1_s1, xor_4bits_1_s1;

  AND_4BITS and_4bits_1 (.A(A), .B(B), .S1(and_4bits_1_s1));
  OR_4BITS or_4bits_1 (.A(A), .B(B), .S1(or_4bits_1_s1));
  XOR_4BITS xor_4bits_1 (.A(A), .B(B), .S1(xor_4bits_1_s1));
  ADD_4BITS add_4bits_1 (.C_in(Carry_Flag), .A(A), .B(B), .S(add_4bits_1_s), .C_out(Carry_Flag_2));
  Multiplexer #(.select(2), .width(4), .enable("false")) multiplexer_1 (
    .in0(and_4bits_1_s1), .in1(or_4bits_1_s1), .in2(xor_4bits_1_s1), .in3(add_4bits_1_s), .out(S1),
    .sel(OPERATIONS));
endmodule

module REGISTERS_4BITS (
  input  Clock,
  input  [3:0] A,
  input  Enable,
  input  [3:0] B,
  output [3:0] S1
);

  S_R_Flip_Flop s_r_ff_1 (.S(A[0]), .clk(Clock), .R(B[0]), .Q(S1[0]), .en(Enable));  // open: Qn, preset, reset
  S_R_Flip_Flop s_r_ff_2 (.S(A[1]), .clk(Clock), .R(B[1]), .Q(S1[1]), .en(Enable));  // open: Qn, preset, reset
  S_R_Flip_Flop s_r_ff_3 (.S(A[2]), .clk(Clock), .R(B[2]), .Q(S1[2]), .en(Enable));  // open: Qn, preset, reset
  S_R_Flip_Flop s_r_ff_4 (.S(A[3]), .clk(Clock), .R(B[3]), .Q(S1[3]), .en(Enable));  // open: Qn, preset, reset
endmodule

// REGISTERS
module _4_REGISTERS_4BITS (
  input  Clock,
  input  [3:0] UAL_ENTRY,
  input  [1:0] SELECTION_OUTPUT_1,
  input  [1:0] Choix_registre_input,
  input  [1:0] SELECTION_OUTPUT_2,
  input  [3:0] RESET,
  input  Enable_Write_Register,
  output [3:0] S1,
  output [3:0] S2
);

  wire demultiplexer_2_out0, demultiplexer_2_out1, demultiplexer_2_out2, demultiplexer_2_out3;
  wire [3:0] demultiplexer_1_out0, demultiplexer_1_out1, demultiplexer_1_out2, demultiplexer_1_out3,
       registers_4bits_1_s1, registers_4bits_2_s1, registers_4bits_3_s1, registers_4bits_4_s1;

  Demultiplexer #(.select(2), .width(4), .enable("false")) demultiplexer_1 (
    .out0(demultiplexer_1_out0), .out1(demultiplexer_1_out1), .out2(demultiplexer_1_out2),
    .out3(demultiplexer_1_out3), .in(UAL_ENTRY), .sel(Choix_registre_input));
  Demultiplexer #(.select(2), .enable("false")) demultiplexer_2 (
    .out0(demultiplexer_2_out0), .out1(demultiplexer_2_out1), .out2(demultiplexer_2_out2),
    .out3(demultiplexer_2_out3), .in(Enable_Write_Register), .sel(Choix_registre_input));
  REGISTERS_4BITS registers_4bits_1 (
    .A(demultiplexer_1_out0), .Enable(demultiplexer_2_out0), .B(RESET), .Clock(Clock),
    .S1(registers_4bits_1_s1));
  REGISTERS_4BITS registers_4bits_2 (
    .A(demultiplexer_1_out1), .Enable(demultiplexer_2_out1), .B(RESET), .Clock(Clock),
    .S1(registers_4bits_2_s1));
  REGISTERS_4BITS registers_4bits_3 (
    .A(demultiplexer_1_out2), .Enable(demultiplexer_2_out2), .B(RESET), .Clock(Clock),
    .S1(registers_4bits_3_s1));
  REGISTERS_4BITS registers_4bits_4 (
    .A(demultiplexer_1_out3), .Enable(demultiplexer_2_out3), .B(RESET), .Clock(Clock),
    .S1(registers_4bits_4_s1));
  Multiplexer #(.select(2), .width(4)) multiplexer_1 (
    .in0(registers_4bits_1_s1), .in1(registers_4bits_2_s1), .in2(registers_4bits_3_s1),
    .in3(registers_4bits_4_s1), .out(S1), .sel(SELECTION_OUTPUT_1));  // open: en
  Multiplexer #(.select(2), .width(4)) multiplexer_2 (
    .in0(registers_4bits_1_s1), .in1(registers_4bits_2_s1), .in2(registers_4bits_3_s1),
    .in3(registers_4bits_4_s1), .out(S2), .sel(SELECTION_OUTPUT_2));  // open: en

  // Notes on the sheet:
  //   R0
  //   R1
  //   R2
  //   R3
endmodule

module PROCESSOR (
  input  [3:0] WRITE_REG,
  input  [3:0] Adress_RAM,
  input  [1:0] SELECT_INPUT_REG,
  input  Enable_RAM,
  input  load_RAM,
  input  Clock,
  input  [1:0] Choix_registre_input,
  input  clear_RAM,
  input  [3:0] RESET,
  input  ENABLE_WRITE_REGISTER,
  input  [1:0] SELECTION_OUTPUT_1,
  input  [1:0] SELECTION_OUTPUT_2,
  input  [1:0] OPERATIONS
);

  wire [3:0] multiplexer_1_out, n4_registers_4bits_1_s1, n4_registers_4bits_1_s2, ual_4bits_1_s1;

  Multiplexer #(.select(2), .width(4), .enable("false")) multiplexer_1 (
    .in0(ual_4bits_1_s1), .in1(n4_registers_4bits_1_s1), .in2(WRITE_REG), .out(multiplexer_1_out),
    .sel(SELECT_INPUT_REG));  // open: in3
  _4_REGISTERS_4BITS u_4_registers_4bits_1 (
    .UAL_ENTRY(multiplexer_1_out), .Choix_registre_input(Choix_registre_input), .RESET(RESET),
    .Enable_Write_Register(ENABLE_WRITE_REGISTER), .Clock(Clock), .SELECTION_OUTPUT_1(SELECTION_OUTPUT_1),
    .SELECTION_OUTPUT_2(SELECTION_OUTPUT_2), .S1(n4_registers_4bits_1_s1), .S2(n4_registers_4bits_1_s2));
  UAL_4BITS ual_4bits_1 (
    .A(n4_registers_4bits_1_s1), .B(n4_registers_4bits_1_s2), .Carry_Flag(1'b0), .OPERATIONS(OPERATIONS),
    .S1(ual_4bits_1_s1));  // open: Carry_Flag_2
  RAM #(.addrWidth(4), .dataWidth(4)) ram_1 (
    .addr(Adress_RAM), .data(n4_registers_4bits_1_s1), .sel(Enable_RAM), .clk(Clock), .ld(load_RAM),
    .clr(clear_RAM));
endmodule
